# Fritzing sketch Robonox (saved by Fritzing 0.9.4)

parts:
  Raspberry_Pi_1 = Raspberry Pi 3 [part_number=RPI-3-V1.2]
  Relay1 = RELAY [package=OJ]
  Relay2 = RELAY [package=OJ]
  Relay3 = RELAY [package=OJ]
  Stepper_Motor_Driver = Pololu A4988 [package=SO16]

nets:
  N1: Raspberry_Pi_1.GPIO17, Stepper_Motor_Driver.1A
  N2: Raspberry_Pi_1.GPIO27, Stepper_Motor_Driver.1B
  N3: Raspberry_Pi_1.GPIO22, Stepper_Motor_Driver.VDD
  GND: Raspberry_Pi_1.GND, Stepper_Motor_Driver.GND
  N4: Raspberry_Pi_1.GPIO21, Relay1.NO
  N5: Raspberry_Pi_1.GPIO20, Relay1.MAIN
  N6: Raspberry_Pi_1.GPIO16, Relay2.NO
  N7: Raspberry_Pi_1.GPIO12, Relay2.MAIN
  N8: Raspberry_Pi_1.GPIO25, Relay3.NO
  N9: Raspberry_Pi_1.GPIO24, Relay3.MAIN
  N10: Stepper_Motor_Driver.2A, Stepper_Motor_Driver.2B

notes:
  Power Source
  Camera module for Rasberry pie 3
  A4988 Stepper Motor Driver
  Relays
